// Logisim project Matriz_LED-(0_F).circ as structural Verilog
module _0_15 (
  input  E0,
  input  E1,
  input  E2,
  input  E3,
  output S0,
  output S1,
  output S2,
  output S3,
  output S4,
  output S5,
  output S6,
  output S7,
  output S8,
  output S9,
  output Sa,
  output Sb,
  output Sc,
  output Sd,
  output Se,
  output Sf
);

  and _0 (S0, ~E0, ~E1, ~E2, ~E3);  // AND_Gate
  and _1 (S1, E0, ~E1, ~E2, ~E3);  // AND_Gate
  and _2 (S2, ~E0, E1, ~E2, ~E3);  // AND_Gate
  and _3 (S3, E0, E1, ~E2, ~E3);  // AND_Gate
  and _4 (S4, ~E0, ~E1, E2, ~E3);  // AND_Gate
  and _5 (S5, E0, ~E1, E2, ~E3);  // AND_Gate
  and _6 (S6, ~E0, E1, E2, ~E3);  // AND_Gate
  and _7 (S7, E0, E1, E2, ~E3);  // AND_Gate
  and _8 (S8, ~E0, ~E1, ~E2, E3);  // AND_Gate
  and _9 (S9, E0, ~E1, ~E2, E3);  // AND_Gate
  and A (Sa, ~E0, E1, ~E2, E3);  // AND_Gate
  and B (Sb, E0, E1, ~E2, E3);  // AND_Gate
  and C (Sc, ~E0, ~E1, E2, E3);  // AND_Gate
  and D (Sd, E0, ~E1, E2, E3);  // AND_Gate
  and E (Se, ~E0, E1, E2, E3);  // AND_Gate
  and F (Sf, E0, E1, E2, E3);
endmodule
